# Fritzing sketch soundbox (saved by Fritzing 0.5.2b)
breadboards: 2

parts:
  U1 = atmega168
  Programming_header = mystery part, 6 pins [chip_label=ICSP spacing=100mil]
  R1 = Resistor [resistance=1k package=THT]
  R1_2 = Resistor [resistance=1k package=THT]
  R2 = Resistor [resistance=220 package=THT]
  LED1 = green LED - 5mm [package="5 mm [THT]"]
  XTAL1 = Crystal [package=THT]
  R4 = Rotary Potentiometer (Large) [package=THT]
  R5 = Rotary Potentiometer (Large) [package=THT]
  C8 = Ceramic Capacitor [capacitance=100nF rated_voltage=35V package="200 mil [THT, multilayer]"]
  S1 = Pushbutton [package="[THT]"]
  C6 = Ceramic Capacitor [capacitance=100nF rated_voltage=35V package="200 mil [THT, multilayer]"]
  C6_2 = Ceramic Capacitor [capacitance=100nF rated_voltage=35V package="200 mil [THT, multilayer]"]
  C5 = Ceramic Capacitor [capacitance=100nF rated_voltage=35V package="200 mil [THT, multilayer]"]
  C4 = Ceramic Capacitor [capacitance=100nF rated_voltage=35V package="200 mil [THT, multilayer]"]
  C7 = Ceramic Capacitor [capacitance=100nF rated_voltage=35V package="200 mil [THT, multilayer]"]
  IC1 = IC, DIP package, 8 pins [chip_label=LM386 spacing=300mil]
  C9 = Ceramic Capacitor [capacitance=1µF rated_voltage=35V package="100 mil [THT, multilayer]"]
  R6 = Rotary Potentiometer (Large) [package=THT]
  C10 = Ceramic Capacitor
  C11 = Electrolytic Capacitor [capacitance=100nF rated_voltage=35V package="100 mil [THT, electrolytic]"]
  R7 = Resistor [resistance=220 package=THT]
  C13 = Electrolytic Capacitor [capacitance=0.1mF rated_voltage=35V package="100 mil [THT, electrolytic]"]
  C14 = Ceramic Capacitor
  SPKR1 = Loudspeaker
  R8 = Rotary Potentiometer (Large) [package=THT]
  S2 = Pushbutton [package="[THT]"]
  LED3 = RGB LED - (4 legs) [package="5 mm [THT]"]
  R11 = Resistor [resistance=100 package=THT]
  R10 = Resistor [resistance=100 package=THT]
  R9 = Resistor [resistance=180 package=THT]
  C8_2 = Ceramic Capacitor [capacitance=100nF rated_voltage=35V package="200 mil [THT, multilayer]"]

nets:
  N1: U1.connector0, Programming_header.pin3
  N2: U1.connector1, S1.Pin_3, S1.Pin_4
  N3: U1.connector2, S2.Pin_3, S2.Pin_4
  N4: U1.connector8, XTAL1.pin_0, C6.1
  N5: U1.connector9, XTAL1.pin_1, C6_2.0
  N6: U1.connector11, R1.Pin_0
  N7: U1.connector13, R9.Pin_1
  N8: U1.connector14, R10.Pin_1
  N9: U1.connector15, R11.Pin_1
  N10: U1.connector16, Programming_header.pin5
  N11: U1.connector17, Programming_header.pin1
  N12: U1.connector18, Programming_header.pin2
  GND: U1.connector19, U1.connector20, U1.connector21, Programming_header.pin4, Programming_header.pin6, R2.Pin_0, LED1.cathode, R4.leg1, R4.leg2, R5.leg1, R5.leg2, C8.0, C8.1, S1.Pin_1, S1.Pin_2, C6.0, C6_2.1, C5.0, C4.0, C7.0, C7.1, IC1.pin2, IC1.pin4, IC1.pin6, R6.leg2, C10.connector1, C11.-, C14.connector0, SPKR1.pin1, R8.leg1, R8.leg2, S2.Pin_1, S2.Pin_2, LED3.common_anode, C8_2.0, C8_2.1
  N13: U1.connector22, R4.wiper
  N14: U1.connector23, R5.wiper
  N15: U1.connector24, R8.wiper
  N16: R1.Pin_1, R1_2.Pin_0, C4.1
  N17: R1_2.Pin_1, C5.1, C9.1
  N18: R2.Pin_1, LED1.anode
  N19: IC1.pin3, R6.wiper, C10.connector0
  N20: IC1.pin5, R7.Pin_0
  N21: IC1.pin7, C11.+
  N22: C9.0, R6.leg1
  N23: R7.Pin_1, C13.-, C14.connector1
  N24: C13.+, SPKR1.pin2
  N25: LED3.red_cathode, R9.Pin_0
  N26: LED3.green_cathode, R10.Pin_0
  N27: LED3.blue_cathode, R11.Pin_0
